# Fritzing sketch moisture_circuit_lipo (saved by Fritzing 1.0.5)
breadboards: 1

parts:
  U1 = XIAO ESP32C6 [part_number=" XIAO ESP32C6"]
  Capacitive_Soil_Moisture_Sensor1 = DFRobot Capacitive Soil Moisture Sensor V1.0 [part_number=SEN0193]
  R1 = Resistor [tolerance=±1% power=0.25W resistance=220k package=THT]
  R2 = Resistor [tolerance=±1% power=0.25W resistance=220k package=THT]
  U2 = LIPO-2000mAh [package=lipo-2000]

nets:
  N1: U1.D0, R1.Pin_1, R2.Pin_1
  N2: U1.D1, Capacitive_Soil_Moisture_Sensor1.A
  N3: U1.D4, R2.Pin_0, U2.+
  N4: U1.D9, R1.Pin_0, U2.-
  N5: U1.D10, Capacitive_Soil_Moisture_Sensor1.VCC
  GND: U1.GND, Capacitive_Soil_Moisture_Sensor1.GND

custom parts:
  XIAO ESP32C6: XIAO ESP32C6 is a cost-effective MCU based on Espressif’s ESP32-C6. This compact MCU excels in Matter-compliant smart home applications with its support for various wireless connectivity (2.4GHz Wi-Fi 6, BLE 5.0, Zigbee, and Thread). Designed with the thumb-size footprint and a single-sided mount of the XIAO Series, it's perfect for space-limited projects. Encrypted on the chip, the XIAO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
  DFRobot Capacitive Soil Moisture Sensor V1.0: DFRobot Capacitive Soil Moisture Sensor V1.0 This product measures soil moisture levels by capacitive sensing, rather than resistive sensing like other types of moisture sensor. It is made of a corrosion resistant material giving it a long service life. Insert it into soil and impress your friends with the real-time soil moisture data! The product includes an on-board voltage regulator which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
